// Logisim project stack_logical_lite.circ as structural Verilog: 29 circuits, main circuit main
module main (
  input  CLK,
  input  RESET,
  input  [1:0] COMMAND,
  input  [2:0] INDEX,
  input  [3:0] IDATA,
  output [3:0] ODATA
);

  wire [3:0] stack_1_d0, stack_1_d1, stack_1_d2, stack_1_d3, stack_1_d4, stack_1_d5, stack_1_d6, stack_1_d7;

  // Probe on stack_1_d0
  stack stack_1 (
    .CLK(CLK), .RESET(RESET), .COMMAND(COMMAND), .INDEX(INDEX), .IDATA(IDATA), .d0(stack_1_d0),
    .d1(stack_1_d1), .d2(stack_1_d2), .d3(stack_1_d3), .d4(stack_1_d4), .d5(stack_1_d5), .d6(stack_1_d6),
    .d7(stack_1_d7), .ODATA(ODATA));
  // Probe on stack_1_d1
  // Probe on stack_1_d2
  // Probe on stack_1_d3
  // Probe on stack_1_d4
  // Probe on stack_1_d5
  // Probe on stack_1_d6
  // Probe on stack_1_d7
endmodule

module stack (
  input  CLK,
  input  RESET,
  input  [1:0] COMMAND,
  input  [2:0] INDEX,
  input  [3:0] IDATA,
  output [3:0] d0,
  output [3:0] d1,
  output [3:0] d2,
  output [3:0] d3,
  output [3:0] d4,
  output [3:0] d5,
  output [3:0] d6,
  output [3:0] d7,
  output [3:0] ODATA
);

  wire and_1_out, and_2_out, and_3_out, and_4_out, and_5_out, and_6_out, and_7_out, and_8_out, and_9_out,
       current_cell_1_a_o, current_cell_1_b_o, current_cell_1_c_o, multiplexer4_1_o_1, multiplexer4_1_o_2,
       multiplexer4_1_o_3, not_1_out, or_1_out, or_2_out, or_3_out, or_4_out, or_5_out, or_6_out, or_7_out,
       or_8_out, or_9_out, or_10_out, or_11_out, or_12_out, pop_1_a_o, pop_1_b_o, pop_1_c_o, push_1_a_o,
       push_1_b_o, push_1_c_o, push_1_s_0, push_1_s_1, push_1_s_2, push_1_s_3, push_1_s_4, push_1_s_5,
       push_1_s_6, push_1_s_7;
  wire [3:0] and14_1_out_3, and14_2_out_3, and14_3_out_3, and14_4_out_3, and14_5_out_3, and14_6_out_3,
       and14_7_out_3, and14_8_out_3, and14_9_out_3, and14_10_out_3, get_1_out_14, pop_1_out_16, push_1_d_0,
       push_1_d_1, push_1_d_2, push_1_d_3, push_1_d_4, push_1_d_5, push_1_d_6, push_1_d_7;

  multiplexer4 multiplexer4_1 (
    .in_1(COMMAND), .o_1(multiplexer4_1_o_1), .o_2(multiplexer4_1_o_2), .o_3(multiplexer4_1_o_3));  // open: o_0
  or or_1 (or_1_out, and_3_out, and_7_out, and_4_out);
  or or_2 (or_2_out, and_2_out, and_8_out, and_5_out);
  or or_3 (or_3_out, and_1_out, and_9_out, and_6_out);
  and and_1 (and_1_out, push_1_c_o, multiplexer4_1_o_1);
  and and_2 (and_2_out, push_1_b_o, multiplexer4_1_o_1);
  and and_3 (and_3_out, push_1_a_o, multiplexer4_1_o_1);
  and and_4 (and_4_out, pop_1_a_o, multiplexer4_1_o_2);
  and and_5 (and_5_out, pop_1_b_o, multiplexer4_1_o_2);
  and and_6 (and_6_out, pop_1_c_o, multiplexer4_1_o_2);
  and and_7 (and_7_out, current_cell_1_a_o, multiplexer4_1_o_3);
  and and_8 (and_8_out, current_cell_1_b_o, multiplexer4_1_o_3);
  and and_9 (and_9_out, current_cell_1_c_o, multiplexer4_1_o_3);
  current_cell current_cell_1 (
    .CLK(CLK), .a(or_1_out), .b(or_2_out), .c(or_3_out), .a_o(current_cell_1_a_o), .b_o(current_cell_1_b_o),
    .c_o(current_cell_1_c_o));
  get get_1 (
    .a(current_cell_1_a_o), .b(current_cell_1_b_o), .c(current_cell_1_c_o), .in_6(multiplexer4_1_o_3),
    .in_8(INDEX), .out_14(get_1_out_14), .d_0(d0), .d_1(d1), .d_2(d2), .d_3(d3), .d_4(d4), .d_5(d5),
    .d_6(d6), .d_7(d7));
  and14 and14_1 (.d1(CLK), .d4(get_1_out_14), .out_3(and14_1_out_3));
  not not_1 (not_1_out, RESET);
  pop pop_1 (
    .a_c(current_cell_1_a_o), .b_c(current_cell_1_b_o), .c_c(current_cell_1_c_o), .in_7(multiplexer4_1_o_2),
    .a_o(pop_1_a_o), .b_o(pop_1_b_o), .c_o(pop_1_c_o), .out_16(pop_1_out_16), .d_0(d0), .d_1(d1), .d_2(d2),
    .d_3(d3), .d_4(d4), .d_5(d5), .d_6(d6), .d_7(d7));
  and14 and14_2 (.d1(CLK), .d4(pop_1_out_16), .out_3(and14_2_out_3));
  or or_4 (or_4_out, CLK, RESET);
  push push_1 (
    .in_1(multiplexer4_1_o_1), .a_c(current_cell_1_a_o), .b_c(current_cell_1_b_o), .c_c(current_cell_1_c_o),
    .a_o(push_1_a_o), .b_o(push_1_b_o), .c_o(push_1_c_o), .IDATA(IDATA), .d_0(push_1_d_0), .s_0(push_1_s_0),
    .d_1(push_1_d_1), .s_1(push_1_s_1), .d_2(push_1_d_2), .s_2(push_1_s_2), .d_3(push_1_d_3),
    .s_3(push_1_s_3), .d_4(push_1_d_4), .s_4(push_1_s_4), .d_5(push_1_d_5), .s_5(push_1_s_5),
    .d_6(push_1_d_6), .s_6(push_1_s_6), .d_7(push_1_d_7), .s_7(push_1_s_7));
  and14 and14_3 (.d1(not_1_out), .d4(push_1_d_0), .out_3(and14_3_out_3));
  or or_5 (or_5_out, RESET, push_1_s_0);
  and14 and14_4 (.d1(not_1_out), .d4(push_1_d_1), .out_3(and14_4_out_3));
  or or_6 (or_6_out, RESET, push_1_s_1);
  and14 and14_5 (.d1(not_1_out), .d4(push_1_d_2), .out_3(and14_5_out_3));
  or or_7 (or_7_out, RESET, push_1_s_2);
  and14 and14_6 (.d1(not_1_out), .d4(push_1_d_3), .out_3(and14_6_out_3));
  or or_8 (or_8_out, RESET, push_1_s_3);
  and14 and14_7 (.d1(not_1_out), .d4(push_1_d_4), .out_3(and14_7_out_3));
  or or_9 (or_9_out, RESET, push_1_s_4);
  and14 and14_8 (.d1(not_1_out), .d4(push_1_d_5), .out_3(and14_8_out_3));
  or or_10 (or_10_out, RESET, push_1_s_5);
  and14 and14_9 (.d1(not_1_out), .d4(push_1_d_6), .out_3(and14_9_out_3));
  or or_11 (or_11_out, RESET, push_1_s_6);
  and14 and14_10 (.d1(not_1_out), .d4(push_1_d_7), .out_3(and14_10_out_3));
  or or_12 (or_12_out, RESET, push_1_s_7);
  assign ODATA = and14_2_out_3 | and14_1_out_3;  // OR_Gate or_13, 4 bits wide
  memory_cell_1 memory_cell_1_1 (.in_1(and14_3_out_3), .clk(or_4_out), .state(or_5_out), .out_4(d0));
  memory_cell_1 memory_cell_1_2 (.in_1(and14_4_out_3), .clk(or_4_out), .state(or_6_out), .out_4(d1));
  memory_cell_1 memory_cell_1_3 (.in_1(and14_5_out_3), .clk(or_4_out), .state(or_7_out), .out_4(d2));
  memory_cell_1 memory_cell_1_4 (.in_1(and14_6_out_3), .clk(or_4_out), .state(or_8_out), .out_4(d3));
  memory_cell_1 memory_cell_1_5 (.in_1(and14_7_out_3), .clk(or_4_out), .state(or_9_out), .out_4(d4));
  memory_cell_1 memory_cell_1_6 (.in_1(and14_8_out_3), .clk(or_4_out), .state(or_10_out), .out_4(d5));
  memory_cell_1 memory_cell_1_7 (.in_1(and14_9_out_3), .clk(or_4_out), .state(or_11_out), .out_4(d6));
  memory_cell_1 memory_cell_1_8 (.in_1(and14_10_out_3), .clk(or_4_out), .state(or_12_out), .out_4(d7));

  // Notes on the sheet:
  //   your circuit must be here
endmodule

module \bit  (
  input  R,
  input  C,
  input  S,
  output Q,
  output NQ
);

  wire and_1_out, and_2_out, nor_2_out, por_1_out;

  and and_1 (and_1_out, R, C);
  and and_2 (and_2_out, C, S);
  nor nor_1 (Q, NQ, and_1_out);
  nor nor_2 (nor_2_out, and_2_out, Q);
  POR por_1 (.out(por_1_out));
  or or_1 (NQ, nor_2_out, por_1_out);
endmodule

module memory_cell (
  input  a,
  input  b,
  input  c,
  input  d,
  input  clk,
  input  state,
  output a_o,
  output b_0,
  output c_o,
  output d_0
);

  wire and_1_out, and_2_out, and_3_out, and_4_out, and_5_out, and_6_out, and_7_out, and_8_out, not_1_out,
       not_2_out, not_3_out, not_4_out, not_5_out;

  not not_1 (not_1_out, a);
  not not_2 (not_2_out, b);
  not not_3 (not_3_out, c);
  not not_4 (not_4_out, d);
  and and_1 (and_1_out, not_1_out, not_5_out);
  and and_2 (and_2_out, a, not_5_out);
  buf and_3 (and_3_out, not_2_out);  // AND_Gate
  and and_4 (and_4_out, b, not_5_out);
  buf and_5 (and_5_out, not_3_out);  // AND_Gate
  and and_6 (and_6_out, c, not_5_out);
  buf and_7 (and_7_out, not_4_out);  // AND_Gate
  and and_8 (and_8_out, d, not_5_out);
  not not_5 (not_5_out, state);
  \bit  bit_1 (.R(and_1_out), .C(clk), .S(and_2_out), .Q(a_o));  // open: NQ
  \bit  bit_2 (.R(and_3_out), .C(clk), .S(and_4_out), .Q(b_0));  // open: NQ
  \bit  bit_3 (.R(and_5_out), .C(clk), .S(and_6_out), .Q(c_o));  // open: NQ
  \bit  bit_4 (.R(and_7_out), .C(clk), .S(and_8_out), .Q(d_0));  // open: NQ
endmodule

module memory_cell_1 (
  input  [3:0] in_1,
  input  clk,
  input  state,
  output [3:0] out_4
);

  wire and_1_out, and_2_out, and_3_out, and_4_out, and_5_out, and_6_out, and_7_out, and_8_out, not_1_out,
       not_2_out, not_3_out, not_4_out;

  not not_1 (not_1_out, in_1[0]);
  not not_2 (not_2_out, in_1[1]);
  not not_3 (not_3_out, in_1[2]);
  not not_4 (not_4_out, in_1[3]);
  and and_1 (and_1_out, not_1_out, state);
  and and_2 (and_2_out, in_1[0], state);
  and and_3 (and_3_out, not_2_out, state);
  and and_4 (and_4_out, in_1[1], state);
  and and_5 (and_5_out, not_3_out, state);
  and and_6 (and_6_out, in_1[2], state);
  and and_7 (and_7_out, not_4_out, state);
  and and_8 (and_8_out, in_1[3], state);
  \bit  bit_1 (.R(and_1_out), .C(clk), .S(and_2_out), .Q(out_4[0]));  // open: NQ
  \bit  bit_2 (.R(and_3_out), .C(clk), .S(and_4_out), .Q(out_4[1]));  // open: NQ
  \bit  bit_3 (.R(and_5_out), .C(clk), .S(and_6_out), .Q(out_4[2]));  // open: NQ
  \bit  bit_4 (.R(and_7_out), .C(clk), .S(and_8_out), .Q(out_4[3]));  // open: NQ
endmodule

module half_summer (
  input  a,
  input  b,
  output r,
  output c
);

  xor xor_1 (r, a, b);
  and and_1 (c, b, a);
endmodule

module summer (
  input  c,
  input  A,
  input  B,
  output R,
  output C_c
);

  wire half_summer_1_c, half_summer_1_r, half_summer_2_c;

  half_summer half_summer_1 (.a(A), .b(B), .r(half_summer_1_r), .c(half_summer_1_c));
  half_summer half_summer_2 (.a(c), .b(half_summer_1_r), .r(R), .c(half_summer_2_c));
  or or_1 (C_c, half_summer_2_c, half_summer_1_c);
endmodule

module current_cell (
  input  CLK,
  input  a,
  input  b,
  input  c,
  output a_o,
  output b_o,
  output c_o
);

  wire not_1_out, not_2_out, not_3_out;

  not not_1 (not_1_out, a);
  not not_2 (not_2_out, b);
  not not_3 (not_3_out, c);
  bitjk bitjk_1 (.J(not_1_out), .C(CLK), .K(a), .out_4(a_o));
  bitjk bitjk_2 (.J(not_2_out), .C(CLK), .K(b), .out_4(b_o));
  bitjk bitjk_3 (.J(not_3_out), .C(CLK), .K(c), .out_4(c_o));
endmodule

module is_0 (
  input  a,
  input  b,
  input  c,
  output out_4
);

  wire not_1_out, not_2_out, not_3_out;

  not not_1 (not_1_out, a);
  not not_2 (not_2_out, b);
  not not_3 (not_3_out, c);
  and and_1 (out_4, not_1_out, not_2_out, not_3_out);
endmodule

module is_1 (
  input  a,
  input  b,
  input  c,
  output out_4
);

  wire not_1_out, not_2_out;

  not not_1 (not_1_out, b);
  not not_2 (not_2_out, c);
  and and_1 (out_4, a, not_1_out, not_2_out);
endmodule

module is_2 (
  input  a,
  input  b,
  input  c,
  output out_4
);

  wire not_1_out, not_2_out;

  not not_1 (not_1_out, a);
  not not_2 (not_2_out, c);
  and and_1 (out_4, not_1_out, b, not_2_out);
endmodule

module is_3 (
  input  a,
  input  b,
  input  c,
  output out_4
);

  wire not_1_out;

  not not_1 (not_1_out, c);
  and and_1 (out_4, a, b, not_1_out);
endmodule

module is_4 (
  input  a,
  input  b,
  input  c,
  output out_4
);

  wire not_1_out, not_2_out;

  not not_1 (not_1_out, a);
  not not_2 (not_2_out, b);
  and and_1 (out_4, not_1_out, not_2_out, c);
endmodule

module is_5 (
  input  a,
  input  b,
  input  c,
  output out_4
);

  wire not_1_out;

  not not_1 (not_1_out, b);
  and and_1 (out_4, a, not_1_out, c);
endmodule

module is_6 (
  input  a,
  input  b,
  input  c,
  output out_4
);

  wire not_1_out;

  not not_1 (not_1_out, a);
  and and_1 (out_4, not_1_out, b, c);
endmodule

module is_7 (
  input  a,
  input  b,
  input  c,
  output out_4
);

  and and_1 (out_4, a, b, c);
endmodule

module summer_1_3 (
  input  a,
  input  b,
  input  c,
  input  d,
  output out_5,
  output out_6,
  output out_7
);

  wire half_summer_1_c, half_summer_2_c;

  half_summer half_summer_1 (.a(a), .b(b), .r(out_5), .c(half_summer_1_c));
  half_summer half_summer_2 (.a(half_summer_1_c), .b(c), .r(out_6), .c(half_summer_2_c));
  half_summer half_summer_3 (.a(half_summer_2_c), .b(d), .r(out_7));  // open: c
endmodule

module bitjk (
  input  J,
  input  C,
  input  K,
  output out_4
);

  wire and_1_out, and_2_out, bit_1_nq, bit_1_q, bit_2_nq, not_1_out;

  and and_1 (and_1_out, out_4, J);
  and and_2 (and_2_out, K, bit_2_nq);
  not not_1 (not_1_out, C);
  \bit  bit_1 (.R(and_1_out), .C(C), .S(and_2_out), .Q(bit_1_q), .NQ(bit_1_nq));
  \bit  bit_2 (.R(bit_1_nq), .C(not_1_out), .S(bit_1_q), .Q(out_4), .NQ(bit_2_nq));
endmodule

module and14 (
  input  d1,
  input  [3:0] d4,
  output [3:0] out_3
);

  and and_1 (out_3[0], d1, d4[0]);
  and and_2 (out_3[1], d1, d4[1]);
  and and_3 (out_3[2], d1, d4[2]);
  and and_4 (out_3[3], d1, d4[3]);
endmodule

module half_substructor (
  input  A,
  input  B,
  output diff,
  output bor
);

  wire not_1_out;

  xor xor_1 (diff, A, B);
  not not_1 (not_1_out, A);
  and and_1 (bor, not_1_out, B);
endmodule

module substructor_3_1 (
  input  a,
  input  b,
  input  c,
  input  d,
  output a_o,
  output b_o,
  output c_o
);

  wire half_substructor_1_bor, half_substructor_2_bor;

  half_substructor half_substructor_1 (.A(a), .B(d), .diff(a_o), .bor(half_substructor_1_bor));
  half_substructor half_substructor_2 (.A(b), .B(half_substructor_1_bor), .diff(b_o), .bor(half_substructor_2_bor));
  half_substructor half_substructor_3 (.A(c), .B(half_substructor_2_bor), .diff(c_o));  // open: bor
endmodule

module push (
  input  in_1,
  input  a_c,
  input  b_c,
  input  c_c,
  input  [3:0] IDATA,
  output [3:0] d_0,
  output s_0,
  output [3:0] d_1,
  output s_1,
  output [3:0] d_2,
  output s_2,
  output a_o,
  output b_o,
  output c_o,
  output [3:0] d_3,
  output s_3,
  output [3:0] d_4,
  output s_4,
  output [3:0] d_5,
  output s_5,
  output [3:0] d_6,
  output s_6,
  output [3:0] d_7,
  output s_7
);

  wire multiplexer8_1_o_0, multiplexer8_1_o_1, multiplexer8_1_o_2, multiplexer8_1_o_3, multiplexer8_1_o_4,
       multiplexer8_1_o_5, multiplexer8_1_o_6, multiplexer8_1_o_7;

  summer_1_3 summer_1_3_1 (.a(in_1), .b(a_c), .c(b_c), .d(c_c), .out_5(a_o), .out_6(b_o), .out_7(c_o));
  multiplexer8 multiplexer8_1 (
    .a(a_o), .b(b_o), .c(c_o), .o_0(multiplexer8_1_o_0), .o_1(multiplexer8_1_o_1), .o_2(multiplexer8_1_o_2),
    .o_3(multiplexer8_1_o_3), .o_4(multiplexer8_1_o_4), .o_5(multiplexer8_1_o_5), .o_6(multiplexer8_1_o_6),
    .o_7(multiplexer8_1_o_7));
  and14 and14_1 (.d1(multiplexer8_1_o_0), .d4(IDATA), .out_3(d_0));
  and14 and14_2 (.d1(multiplexer8_1_o_1), .d4(IDATA), .out_3(d_1));
  and14 and14_3 (.d1(multiplexer8_1_o_2), .d4(IDATA), .out_3(d_2));
  and14 and14_4 (.d1(multiplexer8_1_o_3), .d4(IDATA), .out_3(d_3));
  and14 and14_5 (.d1(multiplexer8_1_o_4), .d4(IDATA), .out_3(d_4));
  and14 and14_6 (.d1(multiplexer8_1_o_5), .d4(IDATA), .out_3(d_5));
  and14 and14_7 (.d1(multiplexer8_1_o_6), .d4(IDATA), .out_3(d_6));
  and and_1 (s_0, in_1, multiplexer8_1_o_0);
  and and_2 (s_1, in_1, multiplexer8_1_o_1);
  and and_3 (s_2, in_1, multiplexer8_1_o_2);
  and14 and14_8 (.d1(multiplexer8_1_o_7), .d4(IDATA), .out_3(d_7));
  and and_4 (s_3, in_1, multiplexer8_1_o_3);
  and and_5 (s_4, in_1, multiplexer8_1_o_4);
  and and_6 (s_5, in_1, multiplexer8_1_o_5);
  and and_7 (s_6, in_1, multiplexer8_1_o_6);
  and and_8 (s_7, in_1, multiplexer8_1_o_7);
endmodule

module pop (
  input  [3:0] d_0,
  input  [3:0] d_1,
  input  a_c,
  input  b_c,
  input  c_c,
  input  [3:0] d_2,
  input  in_7,
  input  [3:0] d_3,
  input  [3:0] d_4,
  input  [3:0] d_5,
  input  [3:0] d_6,
  input  [3:0] d_7,
  output a_o,
  output b_o,
  output c_o,
  output [3:0] out_16
);

  wire multiplexer8_1_o_0, multiplexer8_1_o_1, multiplexer8_1_o_2, multiplexer8_1_o_3, multiplexer8_1_o_4,
       multiplexer8_1_o_5, multiplexer8_1_o_6, multiplexer8_1_o_7;
  wire [3:0] and14_1_out_3, and14_2_out_3, and14_3_out_3, and14_4_out_3, and14_5_out_3, and14_6_out_3,
       and14_7_out_3, and14_8_out_3, or_1_out;

  substructor_3_1 substructor_3_1_1 (.a(a_c), .b(b_c), .c(c_c), .d(in_7), .a_o(a_o), .b_o(b_o), .c_o(c_o));
  multiplexer8 multiplexer8_1 (
    .a(a_c), .b(b_c), .c(c_c), .o_0(multiplexer8_1_o_0), .o_1(multiplexer8_1_o_1), .o_2(multiplexer8_1_o_2),
    .o_3(multiplexer8_1_o_3), .o_4(multiplexer8_1_o_4), .o_5(multiplexer8_1_o_5), .o_6(multiplexer8_1_o_6),
    .o_7(multiplexer8_1_o_7));
  and14 and14_1 (.d1(multiplexer8_1_o_0), .d4(d_0), .out_3(and14_1_out_3));
  and14 and14_2 (.d1(multiplexer8_1_o_1), .d4(d_1), .out_3(and14_2_out_3));
  and14 and14_3 (.d1(multiplexer8_1_o_2), .d4(d_2), .out_3(and14_3_out_3));
  and14 and14_4 (.d1(multiplexer8_1_o_3), .d4(d_3), .out_3(and14_4_out_3));
  and14 and14_5 (.d1(multiplexer8_1_o_4), .d4(d_4), .out_3(and14_5_out_3));
  and14 and14_6 (.d1(multiplexer8_1_o_5), .d4(d_5), .out_3(and14_6_out_3));
  and14 and14_7 (.d1(multiplexer8_1_o_6), .d4(d_6), .out_3(and14_7_out_3));
  assign or_1_out = and14_1_out_3 | and14_2_out_3 | and14_3_out_3 | and14_4_out_3 | and14_5_out_3 | and14_6_out_3 | and14_7_out_3 | and14_8_out_3;  // OR_Gate or_1, 4 bits wide
  and14 and14_8 (.d1(multiplexer8_1_o_7), .d4(d_7), .out_3(and14_8_out_3));
  and14 and14_9 (.d1(in_7), .d4(or_1_out), .out_3(out_16));
endmodule

module multiplexer4 (
  input  [1:0] in_1,
  output o_0,
  output o_1,
  output o_2,
  output o_3
);

  wire not_1_out, not_2_out, not_3_out, not_4_out;

  not not_1 (not_1_out, in_1[1]);
  not not_2 (not_2_out, in_1[0]);
  not not_3 (not_3_out, in_1[1]);
  not not_4 (not_4_out, in_1[0]);
  and and_1 (o_0, not_1_out, not_2_out);
  and and_2 (o_1, not_3_out, in_1[0]);
  and and_3 (o_2, in_1[1], not_4_out);
  and and_4 (o_3, in_1[1], in_1[0]);
endmodule

module get (
  input  [3:0] d_0,
  input  a,
  input  b,
  input  [3:0] d_1,
  input  c,
  input  in_6,
  input  [3:0] d_2,
  input  [2:0] in_8,
  input  [3:0] d_3,
  input  [3:0] d_4,
  input  [3:0] d_5,
  input  [3:0] d_6,
  input  [3:0] d_7,
  output [3:0] out_14
);

  wire multiplexer8_1_o_0, multiplexer8_1_o_1, multiplexer8_1_o_2, multiplexer8_1_o_3, multiplexer8_1_o_4,
       multiplexer8_1_o_5, multiplexer8_1_o_6, multiplexer8_1_o_7, substrructor_3_3_1_out_3,
       substrructor_3_3_1_out_4, substrructor_3_3_1_out_5;
  wire [3:0] and14_1_out_3, and14_2_out_3, and14_3_out_3, and14_4_out_3, and14_5_out_3, and14_6_out_3,
       and14_7_out_3, and14_9_out_3, or_1_out;

  substrructor_3_3 substrructor_3_3_1 (
    .a({c, b, a}), .b(in_8), .out_3(substrructor_3_3_1_out_3), .out_4(substrructor_3_3_1_out_4),
    .out_5(substrructor_3_3_1_out_5));
  multiplexer8 multiplexer8_1 (
    .a(substrructor_3_3_1_out_3), .b(substrructor_3_3_1_out_4), .c(substrructor_3_3_1_out_5),
    .o_0(multiplexer8_1_o_0), .o_1(multiplexer8_1_o_1), .o_2(multiplexer8_1_o_2), .o_3(multiplexer8_1_o_3),
    .o_4(multiplexer8_1_o_4), .o_5(multiplexer8_1_o_5), .o_6(multiplexer8_1_o_6), .o_7(multiplexer8_1_o_7));
  and14 and14_1 (.d1(multiplexer8_1_o_0), .d4(d_0), .out_3(and14_1_out_3));
  and14 and14_2 (.d1(multiplexer8_1_o_1), .d4(d_1), .out_3(and14_2_out_3));
  and14 and14_3 (.d1(multiplexer8_1_o_2), .d4(d_2), .out_3(and14_3_out_3));
  and14 and14_4 (.d1(multiplexer8_1_o_3), .d4(d_3), .out_3(and14_4_out_3));
  and14 and14_5 (.d1(multiplexer8_1_o_4), .d4(d_4), .out_3(and14_5_out_3));
  and14 and14_6 (.d1(multiplexer8_1_o_5), .d4(d_5), .out_3(and14_6_out_3));
  and14 and14_7 (.d1(multiplexer8_1_o_6), .d4(d_6), .out_3(and14_7_out_3));
  assign or_1_out = and14_1_out_3 | and14_2_out_3 | and14_3_out_3 | and14_4_out_3 | and14_5_out_3 | and14_6_out_3 | and14_7_out_3 | and14_9_out_3;  // OR_Gate or_1, 4 bits wide
  and14 and14_8 (.d1(in_6), .d4(or_1_out), .out_3(out_14));
  and14 and14_9 (.d1(multiplexer8_1_o_7), .d4(d_7), .out_3(and14_9_out_3));
endmodule

module summer_3_3 (
  input  [2:0] a,
  input  [2:0] b,
  output out_3,
  output out_4,
  output out_5
);

  wire half_summer_1_c, summer_1_c_c;

  half_summer half_summer_1 (.a(a[0]), .b(b[0]), .r(out_3), .c(half_summer_1_c));
  summer summer_1 (.c(half_summer_1_c), .A(a[1]), .B(b[1]), .R(out_4), .C_c(summer_1_c_c));
  summer summer_2 (.c(summer_1_c_c), .A(a[2]), .B(b[2]), .R(out_5));  // open: C_c
endmodule

module multiplexer8 (
  input  a,
  input  b,
  input  c,
  output o_0,
  output o_1,
  output o_2,
  output o_3,
  output o_4,
  output o_5,
  output o_6,
  output o_7
);

  is_0 is_0_1 (.a(a), .b(b), .c(c), .out_4(o_0));
  is_1 is_1_1 (.a(a), .b(b), .c(c), .out_4(o_1));
  is_2 is_2_1 (.a(a), .b(b), .c(c), .out_4(o_2));
  is_3 is_3_1 (.a(a), .b(b), .c(c), .out_4(o_3));
  is_4 is_4_1 (.a(a), .b(b), .c(c), .out_4(o_4));
  is_5 is_5_1 (.a(a), .b(b), .c(c), .out_4(o_5));
  is_6 is_6_1 (.a(a), .b(b), .c(c), .out_4(o_6));
  is_7 is_7_1 (.a(a), .b(b), .c(c), .out_4(o_7));
endmodule

module substrructor_3_3 (
  input  [2:0] a,
  input  [2:0] b,
  output out_3,
  output out_4,
  output out_5
);

  wire half_substructor_1_bor, substractor_1_bout;

  half_substructor half_substructor_1 (.A(a[0]), .B(b[0]), .diff(out_3), .bor(half_substructor_1_bor));
  substractor substractor_1 (.a(a[1]), .b(half_substructor_1_bor), .bin(b[1]), .d(out_4), .bout(substractor_1_bout));
  substractor substractor_2 (.a(a[2]), .b(substractor_1_bout), .bin(b[2]), .d(out_5));  // open: bout
endmodule

module substractor (
  input  a,
  input  b,
  input  bin,
  output d,
  output bout
);

  wire half_substructor_1_bor, half_substructor_1_diff, half_substructor_2_bor;

  half_substructor half_substructor_1 (.A(a), .B(b), .diff(half_substructor_1_diff), .bor(half_substructor_1_bor));
  half_substructor half_substructor_2 (.A(half_substructor_1_diff), .B(bin), .diff(d), .bor(half_substructor_2_bor));
  or or_1 (bout, half_substructor_2_bor, half_substructor_1_bor);
endmodule
